# Fritzing sketch Climaduino Thermostat (saved by Fritzing 0.8.3b)
breadboards: 1

parts:
  Part1 = Arduino Uno (Rev3)
  S1 = Round Pushbutton
  S2 = Round Pushbutton
  DHT1 = DHT22 Humidity and Temperature Sensor
  U1 = LCD-16X2 [package=lcd-16x2]
  R2 = Resistor [tolerance=±5% resistance=22k package=THT]
  R1 = Resistor [tolerance=±5% resistance=220 package=THT]

nets:
  GND: Part1.GND, S1.leg1, S2.leg1, U1.VSS, U1.VO, U1.R_W, U1.K, R2.Pin_0
  N1: Part1.D8, U1.DB7
  N2: Part1.D9_PWM, DHT1.DATA
  N3: Part1.D11_PWM/MOSI, S2.leg0
  N4: Part1.D12/MISO, S1.leg0
  N5: Part1.D3_PWM, U1.RS
  N6: Part1.D4, U1.E
  N7: Part1.D5_PWM, U1.DB4
  N8: Part1.D6_PWM, U1.DB5
  N9: Part1.D7, U1.DB6
  VDD: Part1.5V, DHT1.VDD, U1.VDD, R1.Pin_0
  N10: DHT1.GND, R2.Pin_1
  N11: U1.A, R1.Pin_1
